# Fritzing sketch smart-cart-demo-1 (saved by Fritzing 0.9.3b)
breadboards: 1

parts:
  U1 = NodeMCU V1.0
  RDM1 = RDM6300
  LCD1 = LCD screen
  LCM1602_IIC2 = LCM1602 IIC [part_number="LCM1602 IIC" chip_label="LCM1602 IIC" package="DIP (Dual Inline) [THT]"]
  RFID_antenna = RDM6300-ANT

nets:
  N1: U1.D1, LCM1602_IIC2.SCL
  N2: U1.D2, LCM1602_IIC2.SDA
  N3: U1.D3, RDM1.Rx
  N4: U1.D4, RDM1.Tx
  GND: U1.GND, RDM1.GND#3, LCM1602_IIC2.GND
  VIN: U1.Vin, RDM1.5V#4, LCM1602_IIC2.VCC
  N5: RDM1.ANT1, RFID_antenna.ANT1
  N6: RDM1.ANT2, RFID_antenna.ANT2
  VSS: LCD1.VSS, LCM1602_IIC2.VSS
  VDD: LCD1.VDD, LCM1602_IIC2.VDD
  N7: LCD1.V0, LCM1602_IIC2.V0
  N8: LCD1.RS, LCM1602_IIC2.RS
  N9: LCD1.R/W, LCM1602_IIC2.RW
  N10: LCD1.E, LCM1602_IIC2.E
  N11: LCD1.DB0, LCM1602_IIC2.D0
  N12: LCD1.DB1, LCM1602_IIC2.D1
  N13: LCD1.DB2, LCM1602_IIC2.D2
  N14: LCD1.DB3, LCM1602_IIC2.D3
  N15: LCD1.DB4, LCM1602_IIC2.D4
  N16: LCD1.DB5, LCM1602_IIC2.D5
  N17: LCD1.DB6, LCM1602_IIC2.D6
  N18: LCD1.DB7, LCM1602_IIC2.D7
  N19: LCD1.LED+, LCM1602_IIC2.A
  N20: LCD1.LED-, LCM1602_IIC2.K

custom parts:
  NodeMCU V1.0: ESP8266 based NodeMCU
  LCM1602 IIC: I2C-Module to use a 1602 or 2004 LCD on with the wire.h libory Serial LCD Modul
  RDM6300-ANT: Antenna
